# Fritzing sketch Circuit (saved by Fritzing 0.9.5d)
breadboards: 1

parts:
  M1 = DOIT Esp32 DevKit v1 (30 pins long, 11 pins width) [part_number=ESP32S-PIN30]
  M2 = VS1053-mp3-player [package=THT]
  SPKR1 = Loudspeaker  # not connected
  SPKR2 = Loudspeaker  # not connected

nets:
  N1: M1.D5, M2.pin_2
  N2: M1.D18, M2.pin_5
  N3: M1.D19, M2.pin_7
  N4: M1.D23, M2.pin_6
  N5: M1.EN, M2.pin_3
  N6: M1.D35, M2.pin_4
  N7: M1.D33, M2.pin_1

notes:
  5V Source

custom parts:
  DOIT Esp32 DevKit v1 (30 pins long, 11 pins width): The DOIT Esp32 DevKit v1 is one of the development board created by DOIT to evaluate the ESP-WROOM-32 module. It is based on the ESP32 microcontroller that boasts Wifi, Bluetooth, Ethernet and Low Power support all in a single chip. (vanepp) made breadboard work, adjusted pin numbering and labels and reduced size of schematic and cleaned up pcb. This chip is 30pins long (2 x15) and 11 pins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
  VS1053-mp3-player: LC Technology VS1003/1053 MP3 Codec module.
